# Fritzing sketch snarky-doorbell (saved by Fritzing 0.9.3b)
breadboards: 1

parts:
  Raspberry_Pi_1 = Raspberry Pi 3 [part_number=RPI-3-V1.2]
  RE1_VOICE = Rotary Encoder [package=THT]
  LED2_STATUS = RGB LED (com. cathode, rgb) [package="5 mm [THT]"]
  R5 = Resistor [tolerance=±5% resistance=300 package=THT]
  R6 = Resistor [tolerance=±5% resistance=300 package=THT]
  R7 = Resistor [tolerance=±5% resistance=300 package=THT]
  RE2_SETTING = Rotary Encoder [package=THT]
  RE3_VOL = Rotary Encoder [package=THT]
  U1 = RF-LINK_RX [package=rf-link_rx]
  IC2 = atmega328 [package=dip]
  CRYSTAL_1 = CRYSTAL [package=hc49u-v]
  C1 = Ceramic Capacitor [capacitance=22pF package="100 mil [THT, multilayer]"]
  C2 = Ceramic Capacitor [capacitance=22pF package="100 mil [THT, multilayer]"]
  R8 = Resistor [tolerance=±5% resistance=10k package=THT]
  J1 = male pin header, 3 pins [form="♂ (male)"]
  R11 = Resistor [tolerance=±5% resistance=3.3k package=THT]
  R12 = Resistor [tolerance=±5% resistance=2.2k package=THT]
  R13 = Resistor [tolerance=±5% resistance=300 package=THT]
  LED1 = LED - 5mm [color="Red (633nm)" package="5 mm [THT]"]
  R14 = Resistor [tolerance=±5% resistance=3.3k package=THT]
  R15 = Resistor [tolerance=±5% resistance=2.2k package=THT]
  J2 = male pin header, 1 pin [form="♂ (male)"]
  IC3 = attiny85 [package=dip]
  ON/OFF1 = SWITCH_SPDT [package=kps-1290]
  ISP1 = AVR ISP 6 Pin [package=2x3-ns]
  RADIO1 = RF-LINK_TX [package=rf-link_tx]
  R16 = Resistor [tolerance=±5% resistance=300 package=THT]
  LED3 = LED - 5mm [color="Blue (505nm)" package="5 mm [THT]"]
  R17 = Resistor [tolerance=±5% resistance=300 package=THT]
  LED4 = LED - 5mm [color="Green (565nm)" package="5 mm [THT]"]
  TRIGGER1 = male pin header, 3 pins [form="♂ (male)"]
  ANT1 = male pin header, 1 pin [form="♂ (male)"]
  MANUAL1 = Pushbutton [package="[THT]"]
  R18 = Resistor [tolerance=±5% resistance=1k package=THT]

nets:
  N1: Raspberry_Pi_1.GPIO2, RE3_VOL.EncoderPinC
  N2: Raspberry_Pi_1.GPIO3, RE1_VOICE.EncoderPinC
  N3: Raspberry_Pi_1.GIPO4, RE3_VOL.EncoderPinA
  N4: Raspberry_Pi_1.GIPO17, RE3_VOL.EncoderPinB
  N5: Raspberry_Pi_1.GIPO27, RE2_SETTING.EncoderPinA
  N6: Raspberry_Pi_1.GIPO22, RE1_VOICE.EncoderPinB
  N7: Raspberry_Pi_1.GIPO13, R5.Pin_1
  GND: Raspberry_Pi_1.GND, LED2_STATUS.common_cathode, U1.GND, IC2.GND#7, C1.0, C2.0, J1.pin3, R11.Pin_1, R14.Pin_1, IC3.Pin_4, ISP1.6, RADIO1.GND, LED3.cathode, R17.Pin_1, TRIGGER1.pin3, MANUAL1.Pin_3, MANUAL1.Pin_4
  N8: Raspberry_Pi_1.GIPO12, R6.Pin_1
  N9: Raspberry_Pi_1.GIPO23, RE1_VOICE.EncoderPinA
  N10: Raspberry_Pi_1.GIPO18, R7.Pin_1
  N11: Raspberry_Pi_1.GIPO15, RE2_SETTING.EncoderPinB
  N12: Raspberry_Pi_1.GIPO14, RE2_SETTING.EncoderPinC
  N13: LED2_STATUS.red_anode, R5.Pin_0
  N14: LED2_STATUS.green_anode, R7.Pin_0
  N15: LED2_STATUS.blue_anode, R6.Pin_0
  N16: U1.DATA, IC2.D2
  5V: U1.+5V, IC2.VCC, R8.Pin_1, J1.pin2
  N17: IC2.RESET, R8.Pin_0
  N18: IC2.D3_(PWM), R12.Pin_1
  N19: IC2.XLAT1, CRYSTAL_1.1, C1.1
  N20: IC2.XLAT2, CRYSTAL_1.2, C2.1
  N21: IC2.D9_(PWM), R15.Pin_0
  N22: IC2.GND#21, R13.Pin_1
  N23: IC2.A5, LED1.anode
  trig_sig: J1.pin1, R11.Pin_0, R12.Pin_0
  N24: R13.Pin_0, LED1.cathode
  N25: R14.Pin_0, R15.Pin_1, J2.pin1
  N26: IC3.Pin_1, ISP1.5
  N27: IC3.Pin_2, RADIO1.+5V
  N28: IC3.Pin_3, RADIO1.DATA, R16.Pin_0
  N29: IC3.Pin_5, ISP1.4, LED4.anode
  N30: IC3.Pin_6, ISP1.1
  N31: IC3.Pin_7, ISP1.3, R18.Pin_0
  N32: IC3.Pin_8, ON/OFF1.O, ISP1.2, TRIGGER1.pin1
  3.3V: ON/OFF1.P
  N33: RADIO1.ANT, ANT1.pin1
  N34: R16.Pin_1, LED3.anode
  N35: R17.Pin_0, LED4.cathode
  N36: TRIGGER1.pin2, MANUAL1.Pin_1, R18.Pin_1

notes:
  RF receiver module
  RF transmitter module
  RPi3 controller
