# Fritzing sketch snarky-doorbell (saved by Fritzing 0.9.3b)
breadboards: 1

parts:
  Raspberry_Pi_1 = Raspberry Pi 3 [part_number=RPI-3-V1.2]
  RE1_VOICE = Rotary Encoder [package=THT]
  R2 = Resistor [tolerance=±5% resistance=10k package=THT]
  S1_TEST = Pushbutton [package="[THT]"]
  LED2_STATUS = RGB LED (com. cathode, rgb) [package="5 mm [THT]"]
  R5 = Resistor [tolerance=±5% resistance=300 package=THT]
  R6 = Resistor [tolerance=±5% resistance=300 package=THT]
  R7 = Resistor [tolerance=±5% resistance=300 package=THT]
  RE2_STYLE = Rotary Encoder [package=THT]
  RE3_VOL = Rotary Encoder [package=THT]
  U1 = RF-LINK_RX [package=rf-link_rx]
  U2 = RF-LINK_TX [package=rf-link_tx]  # not connected
  IC2 = atmega328 [package=dip]
  CRYSTAL_1 = CRYSTAL [package=hc49u-v]
  C1 = Ceramic Capacitor [capacitance=22pF package="100 mil [THT, multilayer]"]
  C2 = Ceramic Capacitor [capacitance=22pF package="100 mil [THT, multilayer]"]
  R8 = Resistor [tolerance=±5% resistance=10k package=THT]
  J1 = male pin header, 3 pins [form="♂ (male)"]
  R11 = Resistor [tolerance=±5% resistance=3.3k package=THT]
  R12 = Resistor [tolerance=±5% resistance=2.2k package=THT]
  R13 = Resistor [tolerance=±5% resistance=300 package=THT]
  LED1 = LED - 5mm [color="Red (633nm)" package="5 mm [THT]"]
  R14 = Resistor [tolerance=±5% resistance=3.3k package=THT]
  R15 = Resistor [tolerance=±5% resistance=2.2k package=THT]
  J2 = male pin header, 1 pin [form="♂ (male)"]

nets:
  N1: Raspberry_Pi_1.GPIO2, RE3_VOL.EncoderPinC
  N2: Raspberry_Pi_1.GPIO3, RE1_VOICE.EncoderPinC
  N3: Raspberry_Pi_1.GIPO4, RE3_VOL.EncoderPinA
  N4: Raspberry_Pi_1.GIPO17, RE3_VOL.EncoderPinB
  N5: Raspberry_Pi_1.GIPO27, RE2_STYLE.EncoderPinA
  N6: Raspberry_Pi_1.GIPO22, RE1_VOICE.EncoderPinB
  N7: Raspberry_Pi_1.GIPO13, R5.Pin_1
  GND: Raspberry_Pi_1.GND, R2.Pin_0, LED2_STATUS.common_cathode, U1.GND, IC2.GND#7, C1.0, C2.0, J1.pin3, R11.Pin_1, R14.Pin_1
  N8: Raspberry_Pi_1.GIPO12, R6.Pin_1
  N9: Raspberry_Pi_1.GIPO23, RE1_VOICE.EncoderPinA
  N10: Raspberry_Pi_1.GIPO18, R7.Pin_1
  N11: Raspberry_Pi_1.GIPO15, RE2_STYLE.EncoderPinB
  N12: Raspberry_Pi_1.GIPO14, RE2_STYLE.EncoderPinC
  N13: R2.Pin_1, S1_TEST.Pin_3, S1_TEST.Pin_4
  N14: LED2_STATUS.red_anode, R5.Pin_0
  N15: LED2_STATUS.green_anode, R7.Pin_0
  N16: LED2_STATUS.blue_anode, R6.Pin_0
  N17: U1.DATA, IC2.D2
  5V: U1.+5V, IC2.VCC, R8.Pin_1, J1.pin2
  N18: IC2.RESET, R8.Pin_0
  N19: IC2.D3_(PWM), R12.Pin_1
  N20: IC2.XLAT1, CRYSTAL_1.1, C1.1
  N21: IC2.XLAT2, CRYSTAL_1.2, C2.1
  N22: IC2.D9_(PWM), R15.Pin_0
  N23: IC2.GND#21, R13.Pin_1
  N24: IC2.A5, LED1.anode
  trig_sig: J1.pin1, R11.Pin_0, R12.Pin_0
  N25: R13.Pin_0, LED1.cathode
  N26: R14.Pin_0, R15.Pin_1, J2.pin1
